# Fritzing sketch Bluepill_wifi (saved by Fritzing 0.9.3b)
breadboards: 1

parts:
  M1 = BME280
  M2 = ESP-01 Breakout Board Breadboard Adapter [part_number=ESP8266]
  M3 = STM32F103C8T6 blue mini board
  Bauteil3 = USB converter CP2102

nets:
  VIN: M1.VIN, M2.VCC, M3.3.3V, Bauteil3.3V3
  GND: M1.GND, M2.GND, M3.G, Bauteil3.GND
  N1: M1.SCL, M3.B6
  N2: M1.SDA, M3.B7
  N3: M2.TXD, M3.A3
  N4: M2.RXD, M3.A2
  N5: M3.A9, Bauteil3.RXI
  N6: M3.A10, Bauteil3.TXO

custom parts:
  BME280: Temperature Humidity Barometric presure Sensor
  ESP-01 Breakout Board Breadboard Adapter: Generic WiFi Module based on the ESP8266 with onboard PCB antenna and UART communications with breadboard friendly breakout board attached.
