# Fritzing sketch Bluepill_wifi_cp2102_3v3 (saved by Fritzing 0.9.2b)
breadboards: 1

parts:
  M1 = BME280
  M2 = ESP-01 Breakout Board Breadboard Adapter [part_number=ESP8266]
  M3 = BluePill
  U1 = CP2102 USB Module

nets:
  3V3: M1.VIN, M2.VCC, M3.3V3, U1.3V3
  GND: M1.GND, M2.GND, M3.GND, U1.GND
  N1: M1.SCL, M3.B6
  N2: M1.SDA, M3.B7
  N3: M2.TXD, M3.A3
  N4: M2.RXD, M3.A2
  N5: M3.A9, U1.RXD
  N6: M3.A10, U1.TXD

custom parts:
  BME280: Temperature Humidity Barometric presure Sensor
  ESP-01 Breakout Board Breadboard Adapter: Generic WiFi Module based on the ESP8266 with onboard PCB antenna and UART communications with breadboard friendly breakout board attached.
  BluePill: Generic ebay blue pill STM32F103C8 "Blue pill" CPU module. Arm Cortex M3 128KB flash (usually) 20kb ram, RTC on board. Supported by the Arduino IDE for programming. As cheap as an Arduino nano but with more power and memory.
  CP2102 USB Module: 5 Pin USB 2.0 to TTL UART Module Serial Converter CP2102 STC Replace Ft232 Module
